# Fritzing sketch Singing Toy (saved by Fritzing 0.8.7b)
circuit board: 8.46667cm x 5.64444cm
breadboards: 1

parts:
  R1 = Resistor [tolerance=±5% resistance=220 package=THT]
  R2 = Resistor [tolerance=±5% resistance=220 package=THT]
  R3 = Resistor [tolerance=±5% resistance=220 package=THT]
  Green_LED = LED - 5mm [color="Green (555nm)" package="5 mm [THT]"]
  Yellow_LED = LED - 5mm [color="Yellow (595nm)" package="5 mm [THT]"]
  Red_LED = LED - 5mm [color="Red (635nm)" package="5 mm [THT]"]
  Blue_LED = LED - 5mm [color="Blue (470nm)" package="5 mm [THT]"]
  R5 = Resistor [tolerance=±5% resistance=220 package=THT]
  R4 = Trimmer Potentiometer [maximum_resistance=10kΩ package=THT]
  Red_LED1 = LED - 5mm [color="White (4500K)" package="5 mm [THT]"]
  Yellow_LED1 = LED - 5mm [color="Yellow (595nm)" package="5 mm [THT]"]
  Green_LED1 = LED - 5mm [color="Green (555nm)" package="5 mm [THT]"]
  Green_LED2 = LED - 5mm [color="Blue (525nm)" package="5 mm [THT]"]
  Green_LED3 = LED - 5mm [color="White (4500K)" package="5 mm [THT]"]
  R6 = Resistor [tolerance=±5% resistance=220 package=THT]
  R7 = Resistor [tolerance=±5% resistance=220 package=THT]
  R8 = Resistor [tolerance=±5% resistance=220 package=THT]
  R9 = Resistor [tolerance=±5% resistance=220 package=THT]
  R10 = Resistor [tolerance=±5% resistance=220 package=THT]
  Arduino = Arduino Uno (Rev3)
  J1 = Piezo Speaker  # not connected
  R11 = Resistor [tolerance=±5% resistance=1k package=THT]

nets:
  N1: R1.Pin_0, Green_LED.anode
  N2: R1.Pin_1, Arduino.D12/MISO
  N3: R2.Pin_0, Yellow_LED.anode
  N4: R2.Pin_1, Arduino.D11_PWM/MOSI
  N5: R3.Pin_0, Red_LED.anode
  N6: R3.Pin_1, Arduino.D10_PWM/SS
  N7: Green_LED.cathode, Yellow_LED.cathode, Red_LED.cathode, Blue_LED.cathode, R4.leg1, Red_LED1.cathode, Yellow_LED1.cathode, Green_LED1.cathode, Green_LED2.cathode, Green_LED3.cathode, Arduino.GND
  N8: Blue_LED.anode, R5.Pin_0
  N9: R5.Pin_1, Arduino.D13/SCK
  N10: R4.wiper, Arduino.A0
  N11: R4.leg2, Arduino.D8, Arduino.5V, R11.Pin_1
  N12: Red_LED1.anode, R10.Pin_0
  N13: Yellow_LED1.anode, R9.Pin_0
  N14: Green_LED1.anode, R8.Pin_0
  N15: Green_LED2.anode, R7.Pin_0
  N16: Green_LED3.anode, R6.Pin_0
  N17: R6.Pin_1, Arduino.D6_PWM
  N18: R7.Pin_1, Arduino.D5_PWM
  N19: R8.Pin_1, Arduino.D4
  N20: R9.Pin_1, Arduino.D3_PWM
