# Fritzing sketch Wastebin (saved by Fritzing 0.8.7b)
breadboards: 1

parts:
  Part1 = Arduino Mega ADK (Rev3)
  U1 = LCD-16X2 [package=lcd-16x2]
  Part2 = SRF05 Ultrasonic Rangefinder
  R1 = Rotary Potentiometer (Large) [maximum_resistance=100kΩ package=THT]
  R2 = Resistor [package="2512 [SMD]"]
  J1 = Basic Servo
  VCC1 = Battery block 9V

nets:
  N1: Part1.D19/RX1, Part2.Trig
  N2: Part1.D18/TX1, Part2.Echo
  GND: Part1.GND, U1.VSS, U1.R_W, U1.A, Part2.GND, R1.leg1, J1.gnd, VCC1.-
  N3: Part1.D12_PWM, U1.RS
  N4: Part1.D10_PWM, U1.E, J1.pulse
  5V: Part1.5V, U1.VDD, Part2.VCC, R1.leg2, R2.Pin_1
  N5: Part1.D2_PWM, U1.DB7
  N6: Part1.D3_PWM, U1.DB6
  N7: Part1.D4_PWM, U1.DB5
  N8: Part1.D5_PWM, U1.DB4
  N9: U1.VO, R1.wiper
  N10: U1.K, R2.Pin_0

notes:
  Wastebin Wiring
